# Fritzing sketch led-esp8266 (saved by Fritzing 0.9.3b)
breadboards: 1

parts:
  R1 = Resistor [tolerance=±5% resistance=220 package=THT]
  LED1 = LED - 5mm [color="Red (633nm)" package="5 mm [THT]"]
  part = NodeMCU V1.0

nets:
  N1: R1.Pin_0, LED1.anode
  N2: R1.Pin_1, part.D8
  N3: LED1.cathode, part.GND

custom parts:
  NodeMCU V1.0: ESP8266 based NodeMCU
